# Fritzing sketch LCD_backpack_fritzing (saved by Fritzing 0.9.3b)
breadboards: 1

parts:
  U1 = LCD-16X2 [package=lcd-16x2_noholes]  # not connected
  Part1 = Arduino Uno (Rev3)
  R1 = Rotary Potentiometer (Small) [maximum_resistance=100kΩ package=THT]

nets:
  N1: Part1.A3, R1.wiper
  N2: Part1.5V, R1.leg2
  N3: Part1.GND, R1.leg1
