# Fritzing sketch LCD_wiring (saved by Fritzing 0.9.3b)
breadboards: 1

parts:
  U1 = LCD-16X2 [package=lcd-16x2_noholes]
  Part1 = Arduino Uno (Rev3)
  R1 = Rotary Potentiometer (Small) [maximum_resistance=100kΩ package=THT]

nets:
  VSS: U1.VSS, U1.R_W, U1.K, Part1.GND, R1.leg2
  VDD: U1.VDD, U1.A, Part1.5V, R1.leg1
  N1: U1.VO, R1.wiper
  N2: U1.RS, Part1.D7
  N3: U1.E, Part1.D8
  N4: U1.DB4, Part1.D9_PWM
  N5: U1.DB5, Part1.D10_PWM/SS
  N6: U1.DB6, Part1.D11_PWM/MOSI
  N7: U1.DB7, Part1.D12/MISO
