# Fritzing sketch Motor_control_fritizing (saved by Fritzing 0.9.3b)
breadboards: 1

parts:
  Part1 = Arduino Uno (Rev3)
  R1 = Rotary Potentiometer (Small) [maximum_resistance=100kΩ package=THT]
  M1 = DC Motor
  D1 = Rectifier Diode [part_number=1N4001 package="300 mil [THT]"]
  Q1 = NPN-Transistor [package="TO92 [THT]"]
  R2 = Resistor [tolerance=±5% resistance=220 package=THT]

nets:
  N1: Part1.A0, Q1.E
  N2: Part1.A3, R1.wiper
  N3: Part1.5V, R1.leg1, R1.leg2
  N4: Part1.GND, R2.Pin_0
  N5: M1.pin_1, D1.anode
  N6: M1.pin_2, D1.cathode, Q1.C
  N7: Q1.B, R2.Pin_1
