# Fritzing sketch Photointerrupter_fritzing (saved by Fritzing 0.9.3b)
breadboards: 1

parts:
  J1 = Infrared Proximity Sensor
  Part1 = Arduino Uno (Rev3)

nets:
  N1: J1.Vout, Part1.GND
  N2: J1.GND, Part1.D6_PWM
  VCC: J1.Vcc, Part1.5V
